// Logisim project 3bit_parity.circ as structural Verilog: 1 circuit, main circuit Parity_Generator_Checker
module Parity_Generator_Checker (
  input  A,
  input  B,
  input  C,
  input  P_in,
  output P__Parity_Out,
  output E__Error
);

  wire xor_1_p3, xor_2_p3, xor_4_p6;
  wire [1:1] xor_3_p6;

  // XOR_Gate xor_1: pin names not known; wires that end beside it: A, B, xor_1_p3
  // XOR_Gate xor_2: pin names not known; wires that end beside it: A, B, xor_2_p3
  // XOR_Gate xor_3: pin names not known; wires that end beside it: A, B, xor_1_p3, xor_1_p3, C, {xor_3_p6[1], P__Parity_Out}
  // XOR_Gate xor_4: pin names not known; wires that end beside it: A, B, xor_2_p3, xor_2_p3, C, xor_4_p6
  // XOR_Gate xor_5: pin names not known; wires that end beside it: xor_4_p6, {xor_3_p6[1], P__Parity_Out}, E__Error
  // Pins of 1 and 2 bits meet at {xor_3_p6[1], P__Parity_Out}

  assign P_in = C;
endmodule
